# Fritzing sketch two_leds_and_buzzer (saved by Fritzing 0.9.3b)
breadboards: 1

parts:
  부품1 = Arduino Uno (Rev3)
  R1 = Resistor [tolerance=±5% resistance=220 package=THT]
  R2 = Resistor [tolerance=±5% resistance=220 package=THT]
  LED1 = smd LED [color="Red (633nm)" package="0805 [SMD]"]
  LED2 = smd LED [color="Green (570nm)" package="0805 [SMD]"]
  SPKR1 = Loudspeaker [part_number=active]

nets:
  N1: 부품1.D8, R1.Pin_1
  N2: 부품1.D9_PWM, R2.Pin_0
  N3: 부품1.D7, SPKR1.pin2
  N4: 부품1.GND, LED1.cathode, LED2.cathode, SPKR1.pin1
  N5: R1.Pin_0, LED2.anode
  N6: R2.Pin_1, LED1.anode
